# Fritzing sketch flora2 (saved by Fritzing 0.9.4)
circuit board: 7.57836cm x 8.95cm
perfboards: 1

parts:
  R2 = Resistor [tolerance=±5% resistance=470 package=THT]
  R3 = Resistor [tolerance=±5% resistance=470 package=THT]
  R4 = Resistor [tolerance=±5% resistance=330 package=THT]
  R5 = Resistor [tolerance=±5% resistance=330 package=THT]
  R6 = Resistor [tolerance=±5% resistance=560 package=THT]
  R7 = Resistor [tolerance=±5% resistance=560 package=THT]
  J5 = Terminal Block - 3 pins [part_number=Pump package=THT]
  R8 = Resistor [tolerance=±5% resistance=10k package=THT]
  J3 = Terminal Block - 3 pins [part_number="Moisture Sensors A" package=THT]
  J4 = Terminal Block - 3 pins [part_number="Moisture Sensors B" package=THT]
  R18 = Resistor [tolerance=±5% resistance=100 package=THT]
  Q2 = Basic FET N-Channel [part_number=BTS117 package="TO220 [THT]"]
  Q4 = MOSFET-NCHANNEL [part_number=ZVP2106A package=to-92]
  J2 = Terminal Block - 3 pins [part_number="Tank Sensors" package=THT]
  J1 = Terminal Block - 3 pins [part_number=Power package=THT]
  Q3 = MOSFET-NCHANNEL [part_number=ZVN4206A package=to-92]
  Q1 = Basic FET N-Channel [part_number=BTS117 package="TO220 [THT]"]
  J6 = female pin header, 6 pins [form="♀ (female)"]
  D2 = Zener Diode [part_number=SMLVT3V3 breakdown_voltage=3.6V package="Melf DO-213 AB [SMD]"]
  D1 = Zener Diode [part_number=SMLVT3V3 breakdown_voltage=3.6V package="Melf DO-213 AB [SMD]"]
  D3 = Zener Diode [part_number=SMLVT3V3 breakdown_voltage=3.6V package="Melf DO-213 AB [SMD]"]
  D4 = Zener Diode [part_number=SMLVT3V3 breakdown_voltage=3.6V package="Melf DO-213 AB [SMD]"]
  J8 = male pin header, 6 pins [form="♂ (male)" part_number=GPIO2]
  R11 = Resistor [tolerance=±1% resistance=330k package=THT]
  R13 = Resistor [tolerance=±1% resistance=330k package=THT]
  R15 = Resistor [tolerance=±1% resistance=330k package=THT]
  R17 = Resistor [tolerance=±1% resistance=330k package=THT]
  R10 = Resistor [tolerance=±1% resistance=220k package=THT]
  R12 = Resistor [tolerance=±1% resistance=220k package=THT]
  R14 = Resistor [tolerance=±1% resistance=220k package=THT]
  R16 = Resistor [tolerance=±1% resistance=220k package=THT]
  U2 = ESP32S-HiLetgo [part_number="ESP32 DevKitC V4"]
  J7 = male pin header, 9 pins [form="♂ (male)" part_number=GPIO1]
  J9 = male pin header, 14 pins [form="♂ (male)" part_number=GPIO3]
  J10 = male pin header, 3 pins [form="♂ (male)" part_number=Sensor_PWR_sel]
  U1 = Voltage Regulator - 5V [part_number=R-78E5.0-0.5 package="TO220 [THT]"]
  C1 = Electrolytic Capacitor [capacitance=10µF voltage=50V part_number=opt. package="100 mil [THT, electrolytic]"]
  C2 = Electrolytic Capacitor [capacitance=1µF voltage=10V part_number=opt. package="100 mil [THT, electrolytic]"]
  R1 = Resistor [tolerance=±5% resistance=10k package=THT]

nets:
  Sensor_PWR: R2.Pin_0, R3.Pin_0, J3.Line_1, J10.pin2
  N1: R2.Pin_1, R4.Pin_0, J2.Line_1
  N2: R3.Pin_1, R5.Pin_0, J2.Line_2
  ESP32_tank_low: R4.Pin_1, R6.Pin_0, U2.GPIO23, J9.pin13
  ESP32_tank_empty: R5.Pin_1, R7.Pin_0, U2.GPIO21, J9.pin11
  GND: R6.Pin_1, R7.Pin_1, J5.Line_3, J4.Line_3, Q2.source, J2.Line_3, J1.Line_2, Q3.S, Q1.source, J6.pin5, D2.anode, D1.anode, D3.anode, D4.anode, J8.pin1, R11.Pin_1, R13.Pin_1, R15.Pin_1, R17.Pin_1, U2.GND, J7.pin1, J9.pin1, U1.GND, C1.-, C2.-, R1.Pin_0
  N3: J5.Line_1, Q1.drain
  N4: J5.Line_2, Q2.drain
  N5: R8.Pin_0, Q4.G, Q3.D
  5V: R8.Pin_1, Q4.S, J1.Line_3, U2.VIN, J10.pin3, U1.output_voltage, C2.+
  N6: J3.Line_2, R10.Pin_0
  N7: J3.Line_3, R12.Pin_0
  N8: J4.Line_1, R14.Pin_0
  N9: J4.Line_2, R16.Pin_0
  ESP32_sensor_en: R18.Pin_0, U2.GPIO27, J7.pin2
  N10: R18.Pin_1, Q3.G, R1.Pin_1
  ESP32_pump2_ctrl: Q2.gate, U2.GPIO18, J9.pin9
  Sensor_PWR_int: Q4.D, J10.pin1
  N11: J1.Line_1, U1.input_voltage, C1.+
  ESP32_pump1_ctrl: Q1.gate, U2.GPIO19, J9.pin10
  3V3: J6.pin1, J6.pin2, J6.pin6, J8.pin6, U2.3.3, J7.pin9, J9.pin14
  I2C1_SDA: J6.pin3, U2.GPIO26, J7.pin3
  I2C1_SCL: J6.pin4, U2.GPIO25, J7.pin4
  ESP32_moisture2: D2.cathode, R13.Pin_0, R12.Pin_1, U2.GPIO35, J7.pin7
  ESP32_moisture1: D1.cathode, R11.Pin_0, R10.Pin_1, U2.GPIO34, J7.pin8
  ESP32_moisture3: D3.cathode, R15.Pin_0, R14.Pin_1, U2.GPIO32, J7.pin6
  ESP32_moisture4: D4.cathode, R17.Pin_0, R16.Pin_1, U2.GPIO33, J7.pin5
  N12: J8.pin2, U2.GPIO13
  N13: J8.pin3, U2.GPIO12
  N14: J8.pin4, U2.GPIO14
  N15: U2.GPIO15, J9.pin2
  N16: U2.GPIO2, J9.pin3
  N17: U2.GPIO0, J9.pin4
  N18: U2.GPIO4, J9.pin5
  N19: U2.GPIO16, J9.pin6
  N20: U2.GPIO17, J9.pin7
  N21: U2.GPIO5, J9.pin8
  N22: U2.GPIO22, J9.pin12

notes:
  GND
  VCC
  SCK/SCL
  SDI/SDA
  CSB
  SDO/ADDR
  Sensor_PWR
  5V
  Tank_low
  Tank_empty
  Pump1_GND
  Pump2_GND
  Flora2, ESP32 Irrigation Controller, 0.9
  12V
  Moisture1
  Moisture2
  Moisture3
  Moisture4
  P1
  P2
  Tank
  L
  E
  Moisture
  Pwr
  1
  2
  3
  4
  ADDR
  SDA
  SCL
  3V3
  SCK
  MISO
  MOSI
  DO
  DI
  CK
  ESP-32S
  19
  38
  20
  ON
  EN
  flora2
  V1.0p1
  (c)02/21
  M. Prinke
  Pumps
  SensPwr
  Soil
  Sens
  Patches p1:
  1. R1 hinzugefügt:
  R1.1->Q3.G R1.2->GND
  2. Q4 Footprint:
  (ist->soll)
  G->D
  S->G
  D->S

custom parts:
  Terminal Block - 3 pins: Generic Screw Terminal 9.5mm
  MOSFET-NCHANNEL: Generic NMOS footprint
  MOSFET-NCHANNEL: Generic NMOS footprint
  ESP32S-HiLetgo: HiLetgo ESP-WROOM-32 ESP32 ESP-32S Development Board 2.4GHz Dual-Mode WiFi + Bluetooth Dual Cores Microcontroller The ESP32 integrated with Antenna switches, RF Balun, power amplifiers, low-noise amplifiers, filters, and management modules, and the entire solution occupies the least area of PCB. 2.4 GHz Wi-Fi plus Bluetooth dual-mode chip, with TSMC Ultra-low power consumption 40nm technology,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
