# Fritzing sketch flora2_rev01 (saved by Fritzing 0.9.4)
perfboards: 1

parts:
  R2 = Resistor [tolerance=±5% resistance=470 package=THT]
  R3 = Resistor [tolerance=±5% resistance=470 package=THT]
  R4 = Resistor [tolerance=±5% resistance=330 package=THT]
  R5 = Resistor [tolerance=±5% resistance=330 package=THT]
  R6 = Resistor [tolerance=±5% resistance=560 package=THT]
  R7 = Resistor [tolerance=±5% resistance=560 package=THT]
  J5 = Terminal Block - 3 pins [part_number=Pump package=THT]
  R8 = Resistor [tolerance=±5% resistance=10k package=THT]
  U2 = ESP32S-HiLetgo [part_number="ESP32 DevKitC V4"]
  J3 = Terminal Block - 3 pins [part_number="Moisture Sensors A" package=THT]
  J4 = Terminal Block - 3 pins [part_number="Moisture Sensors B" package=THT]
  R10 = Resistor [tolerance=±5% resistance=220 package=THT]
  R11 = Resistor [tolerance=±5% resistance=330 package=THT]
  R12 = Resistor [tolerance=±5% resistance=220 package=THT]
  R13 = Resistor [tolerance=±5% resistance=330 package=THT]
  R14 = Resistor [tolerance=±5% resistance=220 package=THT]
  R15 = Resistor [tolerance=±5% resistance=330 package=THT]
  R16 = Resistor [tolerance=±5% resistance=220 package=THT]
  R17 = Resistor [tolerance=±5% resistance=330 package=THT]
  R18 = Resistor [tolerance=±5% resistance=100 package=THT]
  Q2 = Basic FET N-Channel [part_number=BTS117 package="TO220 [THT]"]
  Q4 = MOSFET-NCHANNEL [part_number=ZVP2106A package=to-92]
  D1 = DIODE-ZENER [part_number=SMLVT3V3 package=sod-323]
  D2 = DIODE-ZENER [part_number=SMLVT3V3 package=sod-323]
  D3 = DIODE-ZENER [part_number=SMLVT3V3 package=sod-323]
  D4 = DIODE-ZENER [package=sod-323]
  J2 = Terminal Block - 3 pins [part_number="Tank Sensors" package=THT]
  J1 = Terminal Block - 3 pins [part_number=Power package=THT]
  Q3 = MOSFET-NCHANNEL [part_number=ZVN4206A package=to-92]
  JP1 = Header 6 [part_number="Socket Header" package=1x06_smd_straight_alt]
  Q1 = Basic FET N-Channel [part_number=BTS117 package="TO220 [THT]"]

nets:
  5V: R2.Pin_0, R3.Pin_0, R8.Pin_1, U2.VIN, J3.Line_1, Q4.S, J1.Line_3
  N1: R2.Pin_1, R4.Pin_0, J2.Line_1
  N2: R3.Pin_1, R5.Pin_0, J2.Line_2
  ESP32_tank_low: R4.Pin_1, R6.Pin_0, U2.GPIO23
  ESP32_tank_empty: R5.Pin_1, R7.Pin_0, U2.GPIO21
  GND: R6.Pin_1, R7.Pin_1, J5.Line_3, U2.GND, J4.Line_3, R11.Pin_1, R13.Pin_1, R15.Pin_1, R17.Pin_1, Q2.source, D1.A, D2.A, D3.A, D4.A, J2.Line_3, J1.Line_2, Q3.S, JP1.5, Q1.source
  N3: J5.Line_1, Q1.drain
  N4: J5.Line_2, Q2.drain
  N5: R8.Pin_0, Q4.G, Q3.D
  3V3: U2.3.3, JP1.1, JP1.2, JP1.6
  ESP32_moisture1: U2.GPIO34, R10.Pin_1, R11.Pin_0, D1.C
  ESP32_moisture2: U2.GPIO35, R12.Pin_1, R13.Pin_0, D2.C
  ESP32_moisture3: U2.GPIO32, R14.Pin_1, R15.Pin_0, D3.C
  ESP32_moisture4: U2.GPIO33, R16.Pin_1, R17.Pin_0, D4.C
  I2C1_SCL: U2.GPIO25, JP1.4
  I2C1_SDA: U2.GPIO26, JP1.3
  ESP32_sensor_en: U2.GPIO13, R18.Pin_0
  ESP32_pump2_ctrl: U2.GPIO18, Q2.gate
  ESP32_pump1_ctrl: U2.GPIO19, Q1.gate
  N6: J3.Line_2, R10.Pin_0
  N7: J3.Line_3, R12.Pin_0
  N8: J4.Line_1, R14.Pin_0
  N9: J4.Line_2, R16.Pin_0
  N10: R18.Pin_1, Q3.G
  Sensor_PWR: Q4.D, J1.Line_1

notes:
  GND
  VCC
  SCK/SCL
  SDI/SDA
  CSB
  SDO/ADDR
  Sensor_PWR
  5V
  Tank_low
  Tank_empty
  Pump1_GND
  Pump2_GND
  Flora2, ESP32 Irrigation Controller, 0.1
  Moisture1
  Moisture2
  Moisture3
  Moisture4

custom parts:
  Terminal Block - 3 pins: Generic Screw Terminal 9.5mm
  ESP32S-HiLetgo: HiLetgo ESP-WROOM-32 ESP32 ESP-32S Development Board 2.4GHz Dual-Mode WiFi + Bluetooth Dual Cores Microcontroller The ESP32 integrated with Antenna switches, RF Balun, power amplifiers, low-noise amplifiers, filters, and management modules, and the entire solution occupies the least area of PCB. 2.4 GHz Wi-Fi plus Bluetooth dual-mode chip, with TSMC Ultra-low power consumption 40nm technology,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
  MOSFET-NCHANNEL: Generic NMOS footprint
  MOSFET-NCHANNEL: Generic NMOS footprint
